# Fritzing sketch sketch (saved by Fritzing 0.9.2b)
breadboards: 1

parts:
  Part1 = Arduino Uno (Rev3)
  U1 = Module 4 Relais 5V [package="Module 4 Relais 5V"]
  U2 = HC-SR04 [chip_label=IC package="SIP (Single Inline) [THT]"]
  PCB2 = RTC_DS1302_module
  S1 = Pushbutton [package="[THT]"]
  DS1 = DS18B20 1-Wire Temperature Sensor [part_number=DS18B20]
  R1 = Resistor [tolerance=±5% resistance=4.7k package=THT]
  Part2 = LCD1602-I2C

nets:
  N1: Part1.A4/SDA, Part2.SDA
  N2: Part1.A5/SCL, Part2.SCL
  N3: Part1.D11_PWM/MOSI, PCB2.RST
  N4: Part1.D12/MISO, PCB2.DAT
  N5: Part1.D13/SCK, PCB2.CLK
  N6: Part1.D2, DS1.DQ, R1.Pin_1
  N7: Part1.D3_PWM, S1.Pin_3, S1.Pin_4
  N8: Part1.D4, U2.Trig
  N9: Part1.D5_PWM, U2.Echo
  N10: Part1.D6_PWM, U1.IN1
  VCC: Part1.5V, U1.VCC, U2.Vcc, PCB2.VCC, DS1.VDD, R1.Pin_0, Part2.VCC
  GND: Part1.GND, U1.GND, U2.GND, PCB2.GND, S1.Pin_1, S1.Pin_2, DS1.GND, Part2.GND

custom parts:
  Module 4 Relais 5V: Module 4 Relais 5V 4x SPD-06VDC-SD-C
  HC-SR04: HC-SR04 ultrasound distance sensor
  RTC_DS1302_module: Arduino module DS1302 SPI Real Time Clock
  LCD1602-I2C: A standard character display, usually with 2x16 characters. Comes in many colors with LCM1602 IIC attached.
